# Fritzing sketch DartCounter (saved by Fritzing 0.9.3b)

parts:
  Part1 = Arduino Pro Mini (5V)
  U2 = 7-SEGMENT-DISPLAY [package=7-segment-display]
  U1 = 7-SEGMENT-DISPLAY [package=7-segment-display]
  Part2 = Max Power IR LED Kit
  S1 = Momentary Switch [package=ksa_sealed_tac_switch]
  S2 = Momentary Switch [package=ksa_sealed_tac_switch]
  S3 = Toggle Switch [package=THT]
  VCC1 = Battery block 9V
  R1 = Resistor [tolerance=±5% resistance=1k package=THT]

nets (from the schematic view):
  VCC: Part1.VCC, Part2.VCC, R1.Pin_0
  N1: Part1.A5, S2.4
  N2: Part1.RAW, S3.L1
  GND: Part1.GND, Part2.GND, S1.1, S2.3, VCC1.-
  N3: Part1.A3, U1.D
  N4: Part1.A2, U1.G1
  N5: Part1.A1, U1.DP
  N6: Part1.A0, U2.D
  N7: Part1.SCK, U2.G1
  N8: Part1.MISO, U2.DP
  N9: Part1.MOSI, U2.A
  N10: Part1.D10, U2.G2
  N11: Part1.D9, U2.G
  N12: Part1.D8, U2.E
  N13: Part1.D7, U1.A
  N14: Part1.D6, U1.G2
  N15: Part1.D5, U1.G
  N16: Part1.D4, U1.E
  N17: Part1.D3, S1.4
  N18: Part1.D2, Part2.CONTROL
  N19: U2.C, U1.C, R1.Pin_1
  N20: U2.F, U1.F
